# Fritzing sketch Conexiones pulsera (saved by Fritzing 0.9.3b)
breadboards: 1

parts:
  LED1 = RGB LED (com. anode, rbg) [package="5 mm [THT]"]
  M1 = MAX30102
  TMP1 = TMP006 Temperature Sensor
  U1 = ESP32S-HiLetgo [part_number=ESP32S-HiLetgo]

nets:
  N1: LED1.red_cathode, U1.GPIO34
  N2: LED1.common_anode, U1.GPIO39
  N3: LED1.blue_cathode, U1.GPIO36
  GND: LED1.green_cathode, M1.GND, TMP1.GND, U1.GPIO9
  VIN: M1.VIN, TMP1.VCC, U1.GPIO11
  N4: M1.SCL, TMP1.SCL
  N5: M1.SDA, TMP1.SDA

custom parts:
  MAX30102: Oximeter module using the MAX30102 chip. You may wish to read (and check your module) this post on power problems with these modules: https://reedpaper.wordpress.com/2018/08/22/pulse-oximeter-max30100-max30102-how-to-fix-wrong-board/ . As usual, if you want the mounting holes in pcb, you need to drag a hole over the pad in silkscreen to actually drill the hole (by default they are not drilled)
  TMP006 Temperature Sensor: TMP006 Contact-less Infrared Thermopile Sensor Breakout
  ESP32S-HiLetgo: HiLetgo ESP-WROOM-32 ESP32 ESP-32S Development Board 2.4GHz Dual-Mode WiFi + Bluetooth Dual Cores Microcontroller The ESP32 integrated with Antenna switches, RF Balun, power amplifiers, low-noise amplifiers, filters, and management modules, and the entire solution occupies the least area of PCB. 2.4 GHz Wi-Fi plus Bluetooth dual-mode chip, with TSMC Ultra-low power consumption 40nm technology,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
