# Fritzing sketch esquema server (saved by Fritzing 0.9.3b)

parts:
  U1 = ESP32S-HiLetgo [part_number=ESP32S-HiLetgo]
  DFPlayer_Mini1 = DFPlayer MINI [package="DIP (Dual Inline) [THT]"]
  SP1 = SPEAKER [package=pcb_mount_speaker]

nets:
  N1: U1.GPIO9, DFPlayer_Mini1.GND
  N2: U1.GPIO11, DFPlayer_Mini1.VCC
  N3: U1.GPIO7, DFPlayer_Mini1.RX
  N4: U1.GPIO8, DFPlayer_Mini1.TX
  N5: DFPlayer_Mini1.SPK1, SP1.-
  N6: DFPlayer_Mini1.SPK2, SP1.+

custom parts:
  ESP32S-HiLetgo: HiLetgo ESP-WROOM-32 ESP32 ESP-32S Development Board 2.4GHz Dual-Mode WiFi + Bluetooth Dual Cores Microcontroller The ESP32 integrated with Antenna switches, RF Balun, power amplifiers, low-noise amplifiers, filters, and management modules, and the entire solution occupies the least area of PCB. 2.4 GHz Wi-Fi plus Bluetooth dual-mode chip, with TSMC Ultra-low power consumption 40nm technology,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
  DFPlayer MINI: MP3 module by DFRobot.com for playing Music from an SD-Card. Supports WAV and MP3 files.
